# Fritzing sketch rain_sensor (saved by Fritzing 0.9.1b)
breadboards: 1

parts:
  U1 = atmega328 [package=dip]
  XTAL1 = Crystal [frequency="16 Mhz" package=SMD]
  C2 = Ceramic Capacitor [capacitance=22pF package="200 mil [THT, multilayer]"]
  C3 = Ceramic Capacitor [capacitance=22pF package="200 mil [THT, multilayer]"]
  4_5V_(3x1_5V_AA) = 4 x AAA Battery Mount
  ANT1 = Antenna
  J1 = AVR ISP 6 Pin [package=2x3-ns]
  U2 = RF-LINK_TX [package=rf-link_tx]
  R1 = Resistor [tolerance=±5% resistance=10k package=THT]
  D1 = Rectifier Diode [package="Melf DO-213 AA [SMD]"]
  S1 = Pushbutton [package=THT]
  JP1 = Header 2 [package=molex-1x2_lock]
  R2 = Resistor [tolerance=±5% resistance=10k package="1206 [SMD]"]

nets:
  N1: U1.RESET, J1.5, R1.Pin_1, D1.anode, S1.leg1
  N2: U1.D2, JP1.2, R2.Pin_0
  N3: U1.VCC, 4_5V_(3x1_5V_AA).+, J1.2, R1.Pin_0, D1.cathode, JP1.1
  N4: U1.GND, C2.0, C3.0, 4_5V_(3x1_5V_AA).-, J1.6, S1.leg0, R2.Pin_1
  N5: U1.XLAT1, XTAL1.pin_0, C3.1
  N6: U1.XLAT2, XTAL1.pin_1, C2.1
  N7: U1.D5_(PWM), U2.GND
  N8: U1.D6_(PWM), U2.+5V
  N9: U1.D7, U2.DATA
  N10: U1.D11_(PWM), J1.4
  N11: U1.D12, J1.1
  N12: U1.D13, J1.3
  N13: ANT1.antenna_lead, U2.ANT

notes:
  4,5V (3x1,5V AA)
  To tipping bucket
