# Fritzing sketch txrx (saved by Fritzing 0.9.1b)
breadboards: 1

parts:
  U1 = RF-LINK_RX [package=rf-link_rx]
  U2 = RF-LINK_TX [package=rf-link_tx]
  ANT1 = Antenna
  ANT2 = Antenna
  R1 = Resistor [tolerance=±5% resistance=680 package=THT]
  LED1 = LED - 5mm [color="Red (633nm)" package="5 mm [THT]"]
  LED2 = LED - 5mm [color="White (4500K)" package="5 mm [THT]"]
  LED3 = LED - 5mm [color="Blue (430nm)" package="5 mm [THT]"]
  LED4 = LED - 5mm [color="Green (565nm)" package="5 mm [THT]"]
  LED5 = LED - 5mm [color="Yellow (595nm)" package="5 mm [THT]"]
  R2 = Resistor [tolerance=±5% resistance=680 package=THT]
  R3 = Resistor [tolerance=±5% resistance=680 package=THT]
  R4 = Resistor [tolerance=±5% resistance=680 package=THT]
  R5 = Resistor [tolerance=±5% resistance=680 package=THT]
  Part1 = Arduino Uno (Rev3)

nets:
  GND: U1.GND, U2.GND, R1.Pin_0, R2.Pin_0, R3.Pin_0, R4.Pin_0, R5.Pin_0, Part1.GND
  N1: U1.DATA, Part1.D8, Part1.D2
  +5V: U1.+5V, U2.+5V, Part1.5V
  N2: U1.ANT, ANT1.antenna_lead
  N3: U2.ANT, ANT2.antenna_lead
  N4: U2.DATA, Part1.D11_PWM/MOSI
  N5: R1.Pin_1, LED5.cathode
  N6: LED1.cathode, R2.Pin_1
  N7: LED1.anode, Part1.D7
  N8: LED2.cathode, R3.Pin_1
  N9: LED2.anode, Part1.D6_PWM
  N10: LED3.cathode, LED3.anode, R4.Pin_1, Part1.D5_PWM
  N11: LED4.cathode, R5.Pin_1
  N12: LED4.anode, Part1.D4
  N13: LED5.anode, Part1.D3_PWM
